# Fritzing sketch air board (saved by Fritzing 0.7.12b)
breadboards: 1

parts:
  R1 = Resistor [tolerance=±5% resistance=1k package=THT]
  R2 = Resistor [tolerance=±5% resistance=1k package=THT]
  C1 = Ceramic Capacitor [capacitance=100nF package="100 mil [THT, multilayer]"]
  Q2 = 2SC1815 [package="TO92 [THT]"]
  R5 = Resistor [tolerance=±5% resistance=220 package=THT]
  R6 = Resistor [tolerance=±5% resistance=82 package=THT]
  R7 = Resistor [tolerance=±5% resistance=220 package=THT]
  L1 = Inductor [package="400 mil [THT]"]  # not connected
  C2 = Tantalum Capacitor [capacitance="1 μF" package="100 mil [THT, tantalum]"]
  C3 = Tantalum Capacitor [capacitance="1 μF" package="100 mil [THT, tantalum]"]
  D1 = Rectifier Diode [part_number=1N4001 package="300 mil [THT]"]

nets:
  N1: R1.Pin_0, R2.Pin_1, C1.1, Q2.emitter
  N2: Q2.base, R5.Pin_0
  N3: R6.Pin_1, R7.Pin_0
  N4: C2.-, C3.-
  N5: C3.+, D1.cathode

custom parts:
  2SC1815: A standard NPN-transistor
